// Logisim project full_adder_mux_impl.circ as structural Verilog: 1 circuit, main circuit main
module main (
  input  bit_1,
  input  bit_2,
  input  carry_in,
  output sum,
  output carry_out
);

  Multiplexer #(.select(3)) multiplexer_1 (
    .in0(1'b0), .in1(1'b1), .in2(1'b1), .in3(1'b0), .in4(1'b1), .in5(1'b0), .in6(1'b0), .in7(1'b1),
    .out(sum), .sel({carry_in, bit_2, bit_1}));
  Multiplexer #(.select(3)) multiplexer_2 (
    .in0(1'b0), .in1(1'b0), .in2(1'b0), .in3(1'b1), .in4(1'b0), .in5(1'b1), .in6(1'b1), .in7(1'b1),
    .out(carry_out), .sel({carry_in, bit_2, bit_1}));
endmodule
