// Logisim project circuits.circ as structural Verilog: 16 circuits, main circuit mux_intro
module mux_intro (
  input  x1,
  input  x2,
  output y
);

  wire and_1_out, or_1_out;

  and and_1 (and_1_out, x1, x2);
  or or_1 (or_1_out, x1, x2);

  // Notes on the sheet:
  //   How can we connect
  //   them to output
  //   only one at a time?
endmodule

module mux_intro2 (
  input  x1,
  input  x2,
  input  computeOR,
  output y
);

  wire and_1_out, or_1_out;

  and and_1 (and_1_out, x1, x2);
  or or_1 (or_1_out, x1, x2);

  // Notes on the sheet:
  //   How can we connect
  //   them to output
  //   only one at a time?
  //   we want the OR's output
  //   to be connected to y
  //   when computeOR = 1
endmodule

module mux_2x1_impl (
  input  x1,
  input  x2,
  input  computeOR,
  output y
);

  wire and_1_out, and_2_out, and_3_out, not_1_out, or_1_out;

  and and_1 (and_1_out, x1, x2);
  or or_1 (or_1_out, x1, x2);
  not not_1 (not_1_out, computeOR);
  and and_2 (and_2_out, and_1_out, not_1_out);
  and and_3 (and_3_out, or_1_out, computeOR);
  or or_2 (y, and_2_out, and_3_out);
endmodule

module mux_4x1_impl (
  input  x1,
  input  x2,
  input  x3,
  input  x4,
  input  s1,
  input  s2,
  output y
);

  wire multiplexer_1_out, multiplexer_2_out;

  Multiplexer multiplexer_1 (.in0(x1), .in1(x2), .out(multiplexer_1_out), .sel(s1));
  Multiplexer multiplexer_2 (.in0(x3), .in1(x4), .out(multiplexer_2_out), .sel(s1));
  Multiplexer multiplexer_3 (.in0(multiplexer_1_out), .in1(multiplexer_2_out), .out(y), .sel(s2));
endmodule

module mux_3x1_impl (
  input  x1,
  input  x2,
  input  x3,
  input  s1,
  input  s2,
  output y
);

  wire multiplexer_1_out;

  Multiplexer multiplexer_1 (.in0(x1), .in1(x2), .out(multiplexer_1_out), .sel(s1));
  Multiplexer multiplexer_2 (.in0(multiplexer_1_out), .in1(x3), .out(y), .sel(s2));
endmodule

module demux_intro (
  input  x,
  input  s,
  output y1,
  output y2
);


  // Notes on the sheet:
  //   how can we route x to
  //   only one output at a time?
  //   y1 = x, y2 = 0 if s = 0
  //   y1 = 0, y1 = x if s = 1
endmodule

module demux_1x2_intro_impl (
  input  x,
  input  s,
  output y1,
  output y2
);

  wire not_1_out;

  not not_1 (not_1_out, s);
  and and_1 (y1, x, not_1_out);
  and and_2 (y2, x, s);
endmodule

module timing_intro (
  input  x,
  input  y,
  input  z,
  output f
);

  wire and_1_out, and_2_out, and_3_out, not_1_out, not_2_out, not_3_out, or_1_out;

  not not_1 (not_1_out, x);
  not not_2 (not_2_out, y);
  not not_3 (not_3_out, z);
  and and_1 (and_1_out, x, not_2_out);
  and and_2 (and_2_out, not_1_out, y);
  and and_3 (and_3_out, and_2_out, z);
  or or_1 (or_1_out, and_1_out, and_3_out);
  or or_2 (f, or_1_out, not_3_out);
endmodule

module timing_intro2 (
  input  ctrl,
  input  y,
  output f
);

  wire and_1_out, and_2_out, and_3_out, not_1_out, not_2_out, not_3_out, not_4_out, or_1_out;

  not not_1 (not_1_out, ctrl);
  not not_2 (not_2_out, y);
  not not_3 (not_3_out, not_4_out);
  not not_4 (not_4_out, ctrl);
  and and_1 (and_1_out, ctrl, not_2_out);
  and and_2 (and_2_out, not_1_out, y);
  and and_3 (and_3_out, and_2_out, not_4_out);
  or or_1 (or_1_out, and_1_out, and_3_out);
  or or_2 (f, or_1_out, not_3_out);
endmodule

module clock_intro_impl (
  output clk
);

  not not_1 (clk, clk);
endmodule

module clock_intro (
);

  Clock clk ();  // open: out
endmodule

module setup_time (
  input  d,
  output qm,
  output q
);

  wire buffer_1_out, clk_out, nand_1_out, nand_2_out, nand_4_out, nand_5_out, nand_6_out, nand_8_out,
       not_1_out, not_2_out, not_3_out;

  not not_1 (not_1_out, d);
  Clock clk (.out(clk_out));
  not not_2 (not_2_out, clk_out);
  nand nand_1 (nand_1_out, d, not_2_out);
  nand nand_2 (nand_2_out, not_1_out, not_2_out);
  nand nand_3 (qm, nand_1_out, nand_4_out);
  nand nand_4 (nand_4_out, qm, nand_2_out);
  buf buffer_1 (buffer_1_out, qm);
  not not_3 (not_3_out, buffer_1_out);
  nand nand_5 (nand_5_out, buffer_1_out, clk_out);
  nand nand_6 (nand_6_out, not_3_out, clk_out);
  nand nand_7 (q, nand_5_out, nand_8_out);
  nand nand_8 (nand_8_out, q, nand_6_out);
endmodule

module timing_d_latch (
  input  d,
  input  e,
  output q
);

  wire nand_1_out, nand_2_out, nand_4_out, not_1_out;

  not not_1 (not_1_out, d);
  nand nand_1 (nand_1_out, d, e);
  nand nand_2 (nand_2_out, not_1_out, e);
  nand nand_3 (q, nand_1_out, nand_4_out);
  nand nand_4 (nand_4_out, q, nand_2_out);
endmodule

module hold_d_flipflop (
  input  d,
  output qm,
  output q
);

  wire buffer_1_out, clk_out, nand_1_out, nand_2_out, nand_4_out, nand_5_out, nand_6_out, nand_8_out,
       not_1_out, not_2_out, not_3_out;

  not not_1 (not_1_out, d);
  Clock clk (.out(clk_out));
  not not_2 (not_2_out, clk_out);
  nand nand_1 (nand_1_out, d, not_2_out);
  nand nand_2 (nand_2_out, not_1_out, not_2_out);
  nand nand_3 (qm, nand_1_out, nand_4_out);
  nand nand_4 (nand_4_out, qm, nand_2_out);
  buf buffer_1 (buffer_1_out, qm);
  not not_3 (not_3_out, buffer_1_out);
  nand nand_5 (nand_5_out, buffer_1_out, clk_out);
  nand nand_6 (nand_6_out, not_3_out, clk_out);
  nand nand_7 (q, nand_5_out, nand_8_out);
  nand nand_8 (nand_8_out, q, nand_6_out);
endmodule

module setup_d_flipflop (
  input  d,
  output qm,
  output q
);

  wire buffer_1_out, buffer_2_out, clk_out, nand_1_out, nand_2_out, nand_4_out, nand_5_out, nand_6_out,
       nand_8_out, not_1_out, not_2_out, not_3_out;

  Clock clk (.out(clk_out));
  not not_1 (not_1_out, d);
  buf buffer_1 (buffer_1_out, clk_out);
  not not_2 (not_2_out, buffer_1_out);
  nand nand_1 (nand_1_out, d, not_2_out);
  nand nand_2 (nand_2_out, not_1_out, not_2_out);
  nand nand_3 (qm, nand_1_out, nand_4_out);
  nand nand_4 (nand_4_out, qm, nand_2_out);
  buf buffer_2 (buffer_2_out, qm);
  not not_3 (not_3_out, buffer_2_out);
  nand nand_5 (nand_5_out, buffer_2_out, clk_out);
  nand nand_6 (nand_6_out, not_3_out, clk_out);
  nand nand_7 (q, nand_5_out, nand_8_out);
  nand nand_8 (nand_8_out, q, nand_6_out);
endmodule

module setup_timing_2flipflops (
  input  aux,
  input  d,
  output q
);

  wire and_1_out, clk_out, or_1_out, source_q;

  Clock clk (.out(clk_out));
  D_Flip_Flop source (.D(d), .clk(clk_out), .Q(source_q));  // open: Qn, preset, reset
  and and_1 (and_1_out, aux, source_q);
  D_Flip_Flop target (.D(or_1_out), .clk(clk_out), .Q(q));  // open: Qn, preset, reset
  or or_1 (or_1_out, and_1_out, source_q);
endmodule
