// Logisim project chapter_2.circ as structural Verilog: 17 circuits, main circuit c2s3_sop_example
module c2s3_sop_example (
  input  x,
  input  y,
  input  z,
  output f
);

  wire buffer_1_out, buffer_2_out, buffer_3_out, not_1_out, not_2_out, not_3_out, xcyc_out, xcycz_out,
       xycz_out, xyz_out, xyzc_out;

  buf buffer_1 (buffer_1_out, x);
  not not_1 (not_1_out, x);
  buf buffer_2 (buffer_2_out, y);
  not not_2 (not_2_out, y);
  buf buffer_3 (buffer_3_out, z);
  not not_3 (not_3_out, z);
  and xcycz (xcycz_out, not_1_out, not_2_out, buffer_3_out);
  and xcyc (xcyc_out, not_1_out, buffer_2_out, buffer_3_out);
  and xycz (xycz_out, buffer_1_out, not_2_out, buffer_3_out);
  and xyzc (xyzc_out, buffer_1_out, buffer_2_out, not_3_out);
  and xyz (xyz_out, buffer_1_out, buffer_2_out, buffer_3_out);
  or or_1 (f, xcycz_out, xcyc_out, xycz_out, xyzc_out, xyz_out);
endmodule

module c2s3_pos_example (
  input  x,
  input  y,
  input  z,
  output f
);

  wire buffer_1_out, buffer_2_out, buffer_3_out, not_1_out, not_2_out, not_3_out, xcyz_out, xycz_out, xyz_out;

  buf buffer_1 (buffer_1_out, x);
  not not_1 (not_1_out, x);
  buf buffer_2 (buffer_2_out, y);
  not not_2 (not_2_out, y);
  buf buffer_3 (buffer_3_out, z);
  not not_3 (not_3_out, z);
  or xyz (xyz_out, buffer_1_out, buffer_2_out, buffer_3_out);
  or xycz (xycz_out, buffer_1_out, not_2_out, buffer_3_out);
  or xcyz (xcyz_out, not_1_out, buffer_2_out, buffer_3_out);
  and and_1 (f, xyz_out, xycz_out, xcyz_out);
endmodule

module c2s2_not_not_not_x (
  input  x,
  output y
);

  wire not_1_out, not_2_out;

  not not_1 (not_1_out, x);
  not not_2 (not_2_out, not_1_out);
  not not_3 (y, not_2_out);
endmodule

module c3s1_not_gate (
  input  x,
  output not_x
);

  not NOT_GATE (not_x, x);
endmodule

module c3s1_and_gate (
  input  x1,
  input  x2,
  output x1_and_x2
);

  and AND_GATE (x1_and_x2, x1, x2);
endmodule

module c3s1_or_gate (
  input  x1,
  input  x2,
  output x1_or_x2
);

  or OR_GATE (x1_or_x2, x1, x2);
endmodule

module c3s1_nand_gate (
  input  x1,
  input  x2,
  output x1_nand_x2
);

  nand NAND_GATE (x1_nand_x2, x1, x2);
endmodule

module c3s1_xor_gate (
  input  x1,
  input  x2,
  output x1_xor_x2
);

  xor XOR_GATE (x1_xor_x2, x1, x2);
endmodule

module c3s1_nor_gate (
  input  x1,
  input  x2,
  output x1_nor_x2
);

  nor NOR_GATE (x1_nor_x2, x1, x2);
endmodule

module c3s1_xnor_gate (
  input  x1,
  input  x2,
  output x1_nor_x2
);

  wire XOR_GATE_out;

  xor XOR_GATE (XOR_GATE_out, x1, x2);
  not NOT_GATE (x1_nor_x2, XOR_GATE_out);
endmodule

module c4s1_mux (
  input  x1,
  input  x2,
  input  s,
  output y
);

  Multiplexer multiplexer_1 (.in0(x1), .in1(x2), .out(y), .sel(s));
endmodule

module c4s1_demux (
  input  x,
  input  s,
  output y1,
  output y2
);

  Demultiplexer demultiplexer_1 (.out0(y1), .out1(y2), .in(x), .sel(s));
endmodule

module c4s1_mux_impl (
  input  x1,
  input  x2,
  input  s,
  output y
);

  wire and_1_out, and_2_out, not_1_out;

  not not_1 (not_1_out, s);
  and and_1 (and_1_out, x1, not_1_out);
  and and_2 (and_2_out, s, x2);
  or or_1 (y, and_1_out, and_2_out);
endmodule

module c4s1_demux_impl (
  input  x,
  input  s,
  output y1,
  output y2
);

  wire not_1_out;

  not not_1 (not_1_out, s);
  and and_1 (y1, x, not_1_out);
  and and_2 (y2, x, s);
endmodule

module c4s1_encoder_impl (
  input  x3,
  input  x2,
  input  x1,
  input  x0,
  output y1,
  output y0,
  output v
);

  wire and_1_out, and_2_out, and_3_out, and_4_out;

  or or_1 (y1, x3, x2);
  or or_2 (y0, x3, x1);
  and and_1 (and_1_out, x3, ~x2, ~x1, ~x0);  // AND_Gate
  and and_2 (and_2_out, ~x3, x2, ~x1, ~x0);  // AND_Gate
  and and_3 (and_3_out, ~x3, ~x2, x1, ~x0);  // AND_Gate
  and and_4 (and_4_out, ~x3, ~x2, ~x1, x0);  // AND_Gate
  or or_3 (v, and_1_out, and_2_out, and_3_out, and_4_out);
endmodule

module c4s1_priority_encoder_impl (
  input  x3,
  input  x2,
  input  x1,
  input  x0,
  output y1,
  output y0,
  output v
);

  wire and_1_out;

  or or_1 (y1, x3, x2);
  and and_1 (and_1_out, ~x3, ~x2, x1);  // AND_Gate
  or or_2 (v, x3, x2, x1, x0);
  or or_3 (y0, x3, and_1_out);
endmodule

module c4s1_decoder_impl (
  input  x1,
  input  x0,
  output y3,
  output y2,
  output y1,
  output y0
);

  and and_1 (y3, x1, x0);
  and and_2 (y2, x1, ~x0);  // AND_Gate
  and and_3 (y1, ~x1, x0);  // AND_Gate
  and and_4 (y0, ~x1, ~x0);  // AND_Gate
endmodule
