// Logisim project chapter_5.circ as structural Verilog: 10 circuits, main circuit c5s2_sr_latch_impl
module c5s2_sr_latch_impl (
  input  S,
  input  R,
  output Q
);

  wire nand_2_out;

  nand nand_1 (Q, ~S, nand_2_out);  // NAND_Gate
  nand nand_2 (nand_2_out, Q, ~R);  // NAND_Gate
endmodule

module c5s2_d_latch_impl (
  input  D,
  input  E,
  output Q
);

  wire and_1_out, and_2_out;

  and and_1 (and_1_out, D, E);
  and and_2 (and_2_out, ~D, E);  // AND_Gate
  c5s2_sr_latch_impl SR_Latch (.S(and_1_out), .R(and_2_out), .Q(Q));
endmodule

module c5s2_d_flipflop_impl (
  input  D,
  input  clk,
  output Q
);

  wire master_Dlatch_q, not_1_out;

  not not_1 (not_1_out, clk);
  c5s2_d_latch_impl master_Dlatch (.D(D), .E(not_1_out), .Q(master_Dlatch_q));
  c5s2_d_latch_impl slave_Dlatch (.D(master_Dlatch_q), .E(clk), .Q(Q));
endmodule

module c5s2_t_flipflop_impl (
  input  T,
  input  clk,
  output Q
);

  wire multiplexer_1_out, not_1_out;

  Multiplexer multiplexer_1 (.in0(Q), .in1(not_1_out), .out(multiplexer_1_out), .sel(T));
  not not_1 (not_1_out, Q);
  c5s2_d_flipflop_impl D_flipflop (.D(multiplexer_1_out), .clk(clk), .Q(Q));
endmodule

module c5s2_async_d_flipflop_impl (
  input  D,
  input  clk,
  input  R,
  output Q
);

  wire and_1_out, and_2_out, master_Dlatch_q, not_1_out, or_1_out, or_2_out;

  not not_1 (not_1_out, clk);
  and and_1 (and_1_out, D, ~R);  // AND_Gate
  or or_1 (or_1_out, not_1_out, R);
  c5s2_d_latch_impl master_Dlatch (.D(and_1_out), .E(or_1_out), .Q(master_Dlatch_q));
  and and_2 (and_2_out, master_Dlatch_q, ~R);  // AND_Gate
  or or_2 (or_2_out, clk, R);
  c5s2_d_latch_impl slave_Dlatch (.D(and_2_out), .E(or_2_out), .Q(Q));
endmodule

module c5s2_async_jk_flip_flop (
  input  J,
  input  K,
  input  clk,
  input  R,
  output Q
);

  wire multiplexer_1_out, not_1_out;

  not not_1 (not_1_out, Q);
  Multiplexer #(.select(2)) multiplexer_1 (
    .in0(Q), .in1(J), .in2(1'b0), .in3(not_1_out), .out(multiplexer_1_out), .sel({K, J}));
  c5s2_async_d_flipflop_impl c5s2_async_d_flipflop_impl_1 (.D(multiplexer_1_out), .clk(clk), .R(R), .Q(Q));
endmodule

module c5s2_async_t_flipflop_impl (
  input  T,
  input  clk,
  input  in_3,
  output Q
);

  wire multiplexer_1_out, not_1_out;

  Multiplexer multiplexer_1 (.in0(Q), .in1(not_1_out), .out(multiplexer_1_out), .sel(T));
  not not_1 (not_1_out, Q);
  c5s2_async_d_flipflop_impl c5s2_async_d_flipflop_impl_1 (.D(multiplexer_1_out), .clk(clk), .R(in_3), .Q(Q));
endmodule

module c5s4_async_down_counter_impl (
  input  clk,
  input  R,
  output y2,
  output y1,
  output y0
);

  c5s2_async_t_flipflop_impl c5s2_async_t_flipflop_impl_1 (.T(1'b1), .clk(y1), .in_3(R), .Q(y2));
  c5s2_async_t_flipflop_impl c5s2_async_t_flipflop_impl_2 (.T(1'b1), .clk(y0), .in_3(R), .Q(y1));
  c5s2_async_t_flipflop_impl c5s2_async_t_flipflop_impl_3 (.T(1'b1), .clk(clk), .in_3(R), .Q(y0));
endmodule

module c5s4_sync_up_counter_impl (
  input  clk,
  input  R,
  output y2,
  output y1,
  output y0
);

  wire and_1_out;

  and and_1 (and_1_out, y0, y1);
  c5s2_async_t_flipflop_impl c5s2_async_t_flipflop_impl_1 (.T(and_1_out), .clk(clk), .in_3(R), .Q(y2));
  c5s2_async_t_flipflop_impl c5s2_async_t_flipflop_impl_2 (.T(y0), .clk(clk), .in_3(R), .Q(y1));
  c5s2_async_t_flipflop_impl c5s2_async_t_flipflop_impl_3 (.T(1'b1), .clk(clk), .in_3(R), .Q(y0));
endmodule

module c5s4_async_up_counter_impl (
  input  clk,
  input  R,
  output y2,
  output y1,
  output y0
);

  wire not_1_out, not_2_out;

  not not_1 (not_1_out, y1);
  not not_2 (not_2_out, y0);
  c5s2_async_t_flipflop_impl c5s2_async_t_flipflop_impl_1 (.T(1'b1), .clk(not_1_out), .in_3(R), .Q(y2));
  c5s2_async_t_flipflop_impl c5s2_async_t_flipflop_impl_2 (.T(1'b1), .clk(not_2_out), .in_3(R), .Q(y1));
  c5s2_async_t_flipflop_impl c5s2_async_t_flipflop_impl_3 (.T(1'b1), .clk(clk), .in_3(R), .Q(y0));
endmodule
