// Logisim project chapter_6.circ as structural Verilog: 22 circuits, main circuit c6s2_half_adder_impl
module c6s2_half_adder_impl (
  input  in1,
  input  in2,
  output sum,
  output carry
);

  xor xor_1 (sum, in1, in2);
  and and_1 (carry, in1, in2);
endmodule

module c6s2_full_adder_impl (
  input  in1,
  input  in2,
  input  carry_in,
  output sum,
  output carry_out
);

  wire and_1_out, and_2_out, xor_1_out;

  xor xor_1 (xor_1_out, in1, in2);
  and and_1 (and_1_out, in1, in2);
  and and_2 (and_2_out, xor_1_out, carry_in);
  xor xor_2 (sum, xor_1_out, carry_in);
  or or_1 (carry_out, and_1_out, and_2_out);
endmodule

module c6s2_full_adder_4b_impl (
  input  carry_in,
  input  [3:0] x,
  input  [3:0] y,
  output [3:0] x_plus_y,
  output carry_out,
  output overflow
);

  wire c6s2_full_adder_impl_1_carry_out, c6s2_full_adder_impl_2_carry_out, c6s2_full_adder_impl_3_carry_out;

  c6s2_full_adder_impl c6s2_full_adder_impl_1 (
    .in1(x[0]), .in2(y[0]), .carry_in(carry_in), .sum(x_plus_y[0]),
    .carry_out(c6s2_full_adder_impl_1_carry_out));
  c6s2_full_adder_impl c6s2_full_adder_impl_2 (
    .in1(x[1]), .in2(y[1]), .carry_in(c6s2_full_adder_impl_1_carry_out), .sum(x_plus_y[1]),
    .carry_out(c6s2_full_adder_impl_2_carry_out));
  c6s2_full_adder_impl c6s2_full_adder_impl_3 (
    .in1(x[2]), .in2(y[2]), .carry_in(c6s2_full_adder_impl_2_carry_out), .sum(x_plus_y[2]),
    .carry_out(c6s2_full_adder_impl_3_carry_out));
  c6s2_full_adder_impl c6s2_full_adder_impl_4 (
    .in1(x[3]), .in2(y[3]), .carry_in(c6s2_full_adder_impl_3_carry_out), .sum(x_plus_y[3]),
    .carry_out(carry_out));
  xor xor_1 (overflow, c6s2_full_adder_impl_3_carry_out, carry_out);
endmodule

module c6s5_ram_4b_impl (
  input  WE,
  input  RE,
  input  bit_in,
  input  [1:0] addr,
  output bit_out
);

  wire and_1_out, and_2_out, and_3_out, and_4_out, clk_out, d_ff_1_q, d_ff_2_q, d_ff_3_q, d_ff_4_q,
       decoder_1_out0, decoder_1_out1, decoder_1_out2, decoder_1_out3, demultiplexer_1_out0,
       demultiplexer_1_out1, demultiplexer_1_out2, demultiplexer_1_out3, multiplexer_1_out,
       multiplexer_2_out, multiplexer_3_out, multiplexer_4_out, multiplexer_5_out;

  Demultiplexer #(.select(2)) demultiplexer_1 (
    .out0(demultiplexer_1_out0), .out1(demultiplexer_1_out1), .out2(demultiplexer_1_out2),
    .out3(demultiplexer_1_out3), .in(bit_in), .sel(addr));
  Decoder #(.select(2)) decoder_1 (
    .out0(decoder_1_out0), .out1(decoder_1_out1), .out2(decoder_1_out2), .out3(decoder_1_out3), .sel(addr),
    .en(1'b1));
  Multiplexer multiplexer_1 (.in0(d_ff_1_q), .in1(demultiplexer_1_out0), .out(multiplexer_1_out), .sel(and_1_out));
  and and_1 (and_1_out, WE, decoder_1_out0);
  Multiplexer multiplexer_2 (.in0(d_ff_3_q), .in1(demultiplexer_1_out2), .out(multiplexer_2_out), .sel(and_2_out));
  and and_2 (and_2_out, WE, decoder_1_out2);
  Multiplexer multiplexer_3 (.in0(d_ff_2_q), .in1(demultiplexer_1_out1), .out(multiplexer_3_out), .sel(and_3_out));
  and and_3 (and_3_out, WE, decoder_1_out1);
  Multiplexer multiplexer_4 (.in0(d_ff_4_q), .in1(demultiplexer_1_out3), .out(multiplexer_4_out), .sel(and_4_out));
  and and_4 (and_4_out, WE, decoder_1_out3);
  D_Flip_Flop d_ff_1 (.D(multiplexer_1_out), .clk(clk_out), .Q(d_ff_1_q));  // open: Qn, preset, reset
  D_Flip_Flop d_ff_2 (.D(multiplexer_3_out), .clk(clk_out), .Q(d_ff_2_q));  // open: Qn, preset, reset
  D_Flip_Flop d_ff_3 (.D(multiplexer_2_out), .clk(clk_out), .Q(d_ff_3_q));  // open: Qn, preset, reset
  D_Flip_Flop d_ff_4 (.D(multiplexer_4_out), .clk(clk_out), .Q(d_ff_4_q));  // open: Qn, preset, reset
  Clock clk (.out(clk_out));
  Multiplexer #(.select(2)) multiplexer_5 (
    .in0(d_ff_1_q), .in1(d_ff_2_q), .in2(d_ff_3_q), .in3(d_ff_4_q), .out(multiplexer_5_out), .sel(addr));
  and and_5 (bit_out, RE, multiplexer_5_out);
endmodule

module c6s4_alu_4b_impl (
  input  [2:0] inst,
  input  [3:0] a,
  input  [3:0] b,
  output [3:0] c,
  output [3:0] flags
);

  wire [3:0] and_1_out, c6s2_full_adder_4b_impl_1_x_plus_y, not_1_out, or_1_out, undriven, xor_1_out;

  assign not_1_out = ~a;  // NOT_Gate not_1, 4 bits wide
  assign and_1_out = a & b;  // AND_Gate and_1, 4 bits wide
  assign or_1_out = a | b;  // OR_Gate or_1, 4 bits wide
  assign xor_1_out = a ^ b;  // XOR_Gate xor_1, 4 bits wide
  c6s2_full_adder_4b_impl c6s2_full_adder_4b_impl_1 (
    .carry_in(1'b0), .x(b), .y(a), .x_plus_y(c6s2_full_adder_4b_impl_1_x_plus_y), .overflow(flags[3]));  // open: carry_out
  c6s3_comparator_4b_impl c6s3_comparator_4b_impl_1 (.a(a), .b(b), .gt(flags[2]), .lt(flags[1]), .eq(flags[0]));
  Multiplexer #(.select(3), .width(4)) multiplexer_1 (
    .in0(undriven), .in1(c6s2_full_adder_4b_impl_1_x_plus_y), .in2(not_1_out), .in3(and_1_out),
    .in4(or_1_out), .in5(xor_1_out), .in6(4'b0000), .in7(4'b1111), .out(c), .sel(inst));

  // Notes on the sheet:
  //   reserved
endmodule

module c6s3_comparator_4b_impl (
  input  [3:0] a,
  input  [3:0] b,
  output gt,
  output lt,
  output eq
);

  wire and_1_out, and_2_out, and_3_out, and_4_out, and_5_out, and_6_out, c6s3_comparator_impl_1_eq,
       c6s3_comparator_impl_1_gt, c6s3_comparator_impl_1_lt, c6s3_comparator_impl_2_eq,
       c6s3_comparator_impl_2_gt, c6s3_comparator_impl_2_lt, c6s3_comparator_impl_3_eq,
       c6s3_comparator_impl_3_gt, c6s3_comparator_impl_3_lt, c6s3_comparator_impl_4_eq,
       c6s3_comparator_impl_4_gt, c6s3_comparator_impl_4_lt;

  c6s3_comparator_impl c6s3_comparator_impl_1 (
    .in1(a[3]), .in2(b[3]), .gt(c6s3_comparator_impl_1_gt), .lt(c6s3_comparator_impl_1_lt),
    .eq(c6s3_comparator_impl_1_eq));
  c6s3_comparator_impl c6s3_comparator_impl_2 (
    .in1(a[2]), .in2(b[2]), .gt(c6s3_comparator_impl_2_gt), .lt(c6s3_comparator_impl_2_lt),
    .eq(c6s3_comparator_impl_2_eq));
  c6s3_comparator_impl c6s3_comparator_impl_3 (
    .in1(a[1]), .in2(b[1]), .gt(c6s3_comparator_impl_3_gt), .lt(c6s3_comparator_impl_3_lt),
    .eq(c6s3_comparator_impl_3_eq));
  c6s3_comparator_impl c6s3_comparator_impl_4 (
    .in1(a[0]), .in2(b[0]), .gt(c6s3_comparator_impl_4_gt), .lt(c6s3_comparator_impl_4_lt),
    .eq(c6s3_comparator_impl_4_eq));
  and and_1 (and_1_out, c6s3_comparator_impl_1_eq, c6s3_comparator_impl_2_gt);
  and and_2 (and_2_out, c6s3_comparator_impl_1_eq, c6s3_comparator_impl_2_eq, c6s3_comparator_impl_3_gt);
  and and_3 (and_3_out, c6s3_comparator_impl_1_eq, c6s3_comparator_impl_2_eq, c6s3_comparator_impl_3_eq, c6s3_comparator_impl_4_gt);
  and and_4 (and_4_out, c6s3_comparator_impl_1_eq, c6s3_comparator_impl_2_lt);
  and and_5 (and_5_out, c6s3_comparator_impl_1_eq, c6s3_comparator_impl_2_eq, c6s3_comparator_impl_3_lt);
  and and_6 (and_6_out, c6s3_comparator_impl_1_eq, c6s3_comparator_impl_2_eq, c6s3_comparator_impl_3_eq, c6s3_comparator_impl_4_lt);
  and and_7 (eq, c6s3_comparator_impl_1_eq, c6s3_comparator_impl_2_eq, c6s3_comparator_impl_3_eq, c6s3_comparator_impl_4_eq);
  or or_1 (gt, c6s3_comparator_impl_1_gt, and_1_out, and_2_out, and_3_out);
  or or_2 (lt, c6s3_comparator_impl_1_lt, and_4_out, and_5_out, and_6_out);
endmodule

module c6s3_comparator_impl (
  input  in1,
  input  in2,
  output gt,
  output lt,
  output eq
);

  and and_1 (gt, in1, ~in2);  // AND_Gate
  and and_2 (lt, ~in1, in2);  // AND_Gate
  xnor xnor_1 (eq, in1, in2);
endmodule

module c6s6_dx4 (
  input  reset,
  input  [7:0] data,
  input  write,
  input  [7:0] addr
);

  wire alu_bit, and_1_out, and_2_out, and_3_out, and_9_out, and_10_out, and_11_out, and_12_out, and_13_out,
       and_14_out, and_15_out, arg1, arg2, clock_1_out, clock_2_out, clock_3_out, clock_4_out, clock_5_out,
       clock_6_out, clock_7_out, exec, load, load_aluOUT, load_val, or_1_out, or_3_out, RAM_WE, regDA_WE,
       regDI_WE, regDIDA_WE, regFileWE, regOUT_WE, s3, s4, s5, s6, s7, s8, setIP;
  wire [2:0] multiplexer_3_out, multiplexer_4_out, regFileAddr;
  wire [3:0] aluFLG, c6s6_cpu_8b_impl_1_alu_flags, inst;
  wire [7:0] aluOUT, arg1_q, arg2_q, c6s2_full_adder_8b_impl_1_x_plus_y, c6s5_ram_8x8_impl_1_data_out,
       c6s6_cpu_8b_impl_1_alu_out, data_t, ip, memAddr, multiplexer_1_out, multiplexer_2_out,
       multiplexer_5_out, multiplexer_6_out, multiplexer_7_out;

  Multiplexer #(.width(8)) multiplexer_1 (.in0(ip), .in1(data), .out(multiplexer_1_out), .sel(write));
  Multiplexer #(.width(8)) multiplexer_2 (.in0(memAddr), .in1(addr), .out(multiplexer_2_out), .sel(write));
  or or_1 (or_1_out, write, RAM_WE);
  Multiplexer #(.width(3)) multiplexer_3 (.in0(3'b000), .in1(3'b001), .out(multiplexer_3_out), .sel(regDIDA_WE));
  c6s6_stepper_impl c6s6_stepper_impl_1 (
    .reset(reset), .s1(regDI_WE), .s2(s5), .s3(s3), .s4(s7), .s5(regDA_WE), .s6(s6), .s7(s4), .s8(s8));
  and and_1 (and_1_out, s3, regDA_WE);
  c6s5_ram_8x8_impl c6s5_ram_8x8_impl_1 (
    .WE(or_1_out), .RE(1'b1), .data_in(multiplexer_1_out), .addr(multiplexer_2_out),
    .data_out(c6s5_ram_8x8_impl_1_data_out));
  Multiplexer #(.width(3)) multiplexer_4 (
    .in0(multiplexer_3_out), .in1(regFileAddr), .out(multiplexer_4_out), .sel(load));
  Register u_ip (.D(multiplexer_5_out), .en(s8), .clk(clock_1_out), .Q(memAddr), .clr(reset));
  Multiplexer #(.width(8)) multiplexer_5 (
    .in0(c6s2_full_adder_8b_impl_1_x_plus_y), .in1(ip), .out(multiplexer_5_out), .sel(setIP));
  Clock clock_1 (.out(clock_1_out));
  or or_2 (regDIDA_WE, and_1_out, s4);
  Multiplexer #(.width(8)) multiplexer_6 (
    .in0(c6s5_ram_8x8_impl_1_data_out), .in1(aluOUT), .out(multiplexer_6_out), .sel(load_aluOUT));
  Multiplexer #(.width(8)) multiplexer_7 (.in0(multiplexer_6_out), .in1(ip), .out(multiplexer_7_out), .sel(load_val));
  or or_3 (or_3_out, regDI_WE, regFileWE, regDA_WE);
  or or_4 (exec, s6, s5);
  c6s2_full_adder_8b_impl c6s2_full_adder_8b_impl_1 (
    .carry_in(1'b0), .x(memAddr), .y(8'h2), .x_plus_y(c6s2_full_adder_8b_impl_1_x_plus_y));  // open: carry_out, overflow
  c6s6_reg_3x8_impl c6s6_reg_3x8_impl_1 (
    .WE(or_3_out), .RE(1'b1), .data_in(multiplexer_7_out), .addr(multiplexer_4_out), .data_out(data_t));
  Clock clock_2 (.out(clock_2_out));
  and and_2 (and_2_out, arg1, load);
  Clock clock_3 (.out(clock_3_out));
  and and_3 (and_3_out, load, arg2);
  Clock clock_4 (.out(clock_4_out));
  Clock clock_5 (.out(clock_5_out));
  Register u_inst (.D(data_t), .en(s3), .clk(clock_2_out), .Q({regFileAddr, inst, alu_bit}));  // open: clr
  Register u_arg1 (.D(data_t), .en(and_2_out), .clk(clock_3_out), .Q(arg1_q), .clr(reset));
  Register u_arg2 (.D(data_t), .en(and_3_out), .clk(clock_4_out), .Q(arg2_q), .clr(reset));
  Register arg (.D(data_t), .en(s4), .clk(clock_5_out), .Q(ip));  // open: clr
  or or_5 (regOUT_WE, s7, alu_bit);
  or or_6 (load, s8, s7);
  and and_4 (RAM_WE, load, ~alu_bit, ~inst[3], ~inst[2], ~inst[1], inst[0]);  // AND_Gate
  and and_5 (load_aluOUT, load, alu_bit);
  nor nor_1 (regFileWE, load, inst[3], inst[2], inst[0]);
  and and_6 (load_val, ~alu_bit, ~inst[3], inst[2], inst[1], inst[0]);  // AND_Gate
  and and_7 (arg1, ~alu_bit, ~inst[3], inst[2], inst[1], inst[0]);  // AND_Gate
  and and_8 (arg2, ~alu_bit, ~inst[3], inst[2], ~inst[1], ~inst[0]);  // AND_Gate
  c6s6_cpu_8b_impl c6s6_cpu_8b_impl_1 (
    .alu_inst(inst), .alu_in1(arg1_q), .alu_in2(arg2_q), .alu_out(c6s6_cpu_8b_impl_1_alu_out),
    .alu_flags(c6s6_cpu_8b_impl_1_alu_flags));
  Clock clock_6 (.out(clock_6_out));
  Clock clock_7 (.out(clock_7_out));
  Register res (.D(c6s6_cpu_8b_impl_1_alu_out), .en(s5), .clk(clock_6_out), .Q(aluOUT));  // open: clr
  Register #(.width(4)) flg (.D(c6s6_cpu_8b_impl_1_alu_flags), .en(s5), .clk(clock_7_out), .Q(aluFLG));  // open: clr
  and and_9 (and_9_out, ~alu_bit, ~inst[3], inst[2], ~inst[1], inst[0]);  // AND_Gate
  and and_10 (and_10_out, ~alu_bit, ~inst[3], inst[2], inst[1], ~inst[0]);  // AND_Gate
  and and_11 (and_11_out, ~alu_bit, ~inst[3], inst[2], inst[1], inst[0]);  // AND_Gate
  and and_12 (and_12_out, ~alu_bit, inst[3], ~inst[2], ~inst[1], ~inst[0]);  // AND_Gate
  and and_13 (and_13_out, and_10_out, aluFLG[3]);
  and and_14 (and_14_out, and_11_out, aluFLG[2]);
  and and_15 (and_15_out, and_12_out, aluFLG[1]);
  or or_7 (setIP, and_9_out, and_13_out, and_14_out, and_15_out);

  // Other names for the same wires on the sheet: s1 = regDI_WE; s2 = regDA_WE; val[7:0] = ip

  // Notes on the sheet:
  //   fetch
  //   decode
  //   regDI : 000
  //   regDA : 001
  //   regIP : 010
  //   regA : 011
  //   execute
  //   regB : 100
  //   regOUT : 101
  //   regTMP : 110
  //   load
endmodule

module c6s2_full_adder_8b_impl (
  input  carry_in,
  input  [7:0] x,
  input  [7:0] y,
  output [7:0] x_plus_y,
  output carry_out,
  output overflow
);

  wire c6s2_full_adder_4b_impl_1_carry_out;

  c6s2_full_adder_4b_impl c6s2_full_adder_4b_impl_1 (
    .carry_in(carry_in), .x(x[3:0]), .y(y[3:0]), .x_plus_y(x_plus_y[3:0]),
    .carry_out(c6s2_full_adder_4b_impl_1_carry_out));  // open: overflow
  c6s2_full_adder_4b_impl c6s2_full_adder_4b_impl_2 (
    .carry_in(c6s2_full_adder_4b_impl_1_carry_out), .x(x[7:4]), .y(y[7:4]), .x_plus_y(x_plus_y[7:4]),
    .carry_out(carry_out), .overflow(overflow));
endmodule

module c6s5_ram_8x8_impl (
  input  WE,
  input  RE,
  input  [7:0] data_in,
  input  [7:0] addr,
  output [7:0] data_out
);

  wire demultiplexer_1_out0, demultiplexer_1_out1, demultiplexer_1_out2, demultiplexer_1_out3;
  wire [5:0] demultiplexer_2_out0, demultiplexer_2_out1, demultiplexer_2_out2, demultiplexer_2_out3;
  wire [7:0] c6s6_ram_6x8_impl_1_data_out, c6s6_ram_6x8_impl_2_data_out, c6s6_ram_6x8_impl_3_data_out,
       c6s6_ram_6x8_impl_4_data_out;

  Demultiplexer #(.select(2)) demultiplexer_1 (
    .out0(demultiplexer_1_out0), .out1(demultiplexer_1_out1), .out2(demultiplexer_1_out2),
    .out3(demultiplexer_1_out3), .in(WE), .sel(addr[7:6]));
  Demultiplexer #(.select(2), .width(6)) demultiplexer_2 (
    .out0(demultiplexer_2_out0), .out1(demultiplexer_2_out1), .out2(demultiplexer_2_out2),
    .out3(demultiplexer_2_out3), .in(addr[5:0]), .sel(addr[7:6]));
  c6s6_ram_6x8_impl c6s6_ram_6x8_impl_1 (
    .WE(demultiplexer_1_out0), .RE(RE), .data_in(data_in), .addr(demultiplexer_2_out0),
    .data_out(c6s6_ram_6x8_impl_1_data_out));
  c6s6_ram_6x8_impl c6s6_ram_6x8_impl_2 (
    .WE(demultiplexer_1_out1), .RE(RE), .data_in(data_in), .addr(demultiplexer_2_out1),
    .data_out(c6s6_ram_6x8_impl_2_data_out));
  c6s6_ram_6x8_impl c6s6_ram_6x8_impl_3 (
    .WE(demultiplexer_1_out2), .RE(RE), .data_in(data_in), .addr(demultiplexer_2_out2),
    .data_out(c6s6_ram_6x8_impl_3_data_out));
  c6s6_ram_6x8_impl c6s6_ram_6x8_impl_4 (
    .WE(demultiplexer_1_out3), .RE(RE), .data_in(data_in), .addr(demultiplexer_2_out3),
    .data_out(c6s6_ram_6x8_impl_4_data_out));
  Multiplexer #(.select(2), .width(8)) multiplexer_1 (
    .in0(c6s6_ram_6x8_impl_1_data_out), .in1(c6s6_ram_6x8_impl_2_data_out),
    .in2(c6s6_ram_6x8_impl_3_data_out), .in3(c6s6_ram_6x8_impl_4_data_out), .out(data_out), .sel(addr[7:6]));
endmodule

module c6s3_comparator_8b_impl (
  input  [7:0] a,
  input  [7:0] b,
  output gt,
  output lt,
  output eq
);

  wire and_1_out, and_2_out, c6s3_comparator_4b_impl_1_eq, c6s3_comparator_4b_impl_1_gt,
       c6s3_comparator_4b_impl_1_lt, c6s3_comparator_4b_impl_2_eq, c6s3_comparator_4b_impl_2_gt,
       c6s3_comparator_4b_impl_2_lt;

  c6s3_comparator_4b_impl c6s3_comparator_4b_impl_1 (
    .a(a[7:4]), .b(b[7:4]), .gt(c6s3_comparator_4b_impl_1_gt), .lt(c6s3_comparator_4b_impl_1_lt),
    .eq(c6s3_comparator_4b_impl_1_eq));
  c6s3_comparator_4b_impl c6s3_comparator_4b_impl_2 (
    .a(a[3:0]), .b(b[3:0]), .gt(c6s3_comparator_4b_impl_2_gt), .lt(c6s3_comparator_4b_impl_2_lt),
    .eq(c6s3_comparator_4b_impl_2_eq));
  and and_1 (and_1_out, c6s3_comparator_4b_impl_1_eq, c6s3_comparator_4b_impl_2_gt);
  and and_2 (and_2_out, c6s3_comparator_4b_impl_1_eq, c6s3_comparator_4b_impl_2_lt);
  and and_3 (eq, c6s3_comparator_4b_impl_1_eq, c6s3_comparator_4b_impl_2_eq);
  or or_1 (gt, c6s3_comparator_4b_impl_1_gt, and_1_out);
  or or_2 (lt, c6s3_comparator_4b_impl_1_lt, and_2_out);
endmodule

module c6s4_alu_8b_impl (
  input  [3:0] inst,
  input  [7:0] a,
  input  [7:0] b,
  output [7:0] c,
  output [3:0] flags
);

  wire [7:0] add, land, lnot, lor, lxor, neg, undriven, undriven_2, undriven_3;

  assign lnot = ~a;  // NOT_Gate not_1, 8 bits wide
  assign land = a & b;  // AND_Gate and_1, 8 bits wide
  assign lor = a | b;  // OR_Gate or_1, 8 bits wide
  assign lxor = a ^ b;  // XOR_Gate xor_1, 8 bits wide
  c6s2_full_adder_8b_impl c6s2_full_adder_8b_impl_1 (
    .carry_in(1'b0), .x(b), .y(a), .x_plus_y(add), .overflow(flags[3]));  // open: carry_out
  c6s3_comparator_8b_impl c6s3_comparator_8b_impl_1 (.a(a), .b(b), .gt(flags[2]), .lt(flags[1]), .eq(flags[0]));
  c6s2_full_adder_8b_impl c6s2_full_adder_8b_impl_2 (
    .carry_in(1'b1), .x(lnot), .y({8{1'b0}}), .x_plus_y(neg));  // open: carry_out, overflow
  Multiplexer #(.select(4), .width(8)) multiplexer_1 (
    .in0({8{1'b0}}), .in1(add), .in2(neg), .in3(land), .in4(lor), .in5(lxor), .in6(lnot),
    .in7({a[0], a[7:1]}), .in8({a[6:0], a[7]}), .in9({1'b0, a[7:1]}), .in10({a[6:0], 1'b0}),
    .in11({8{1'b0}}), .in12({8{1'b1}}), .in13(undriven), .in14(undriven_2), .in15(undriven_3), .out(c),
    .sel(inst));

  // Other names for the same wires on the sheet: rotl[7:0] = {a[6:0], a[7]}; rotr[7:0] = {a[0], a[7:1]};
  //   shiftl[7:1] = a[6:0]; shiftr[6:0] = a[7:1]

  // Notes on the sheet:
  //   rotl
  //   shiftl
  //   2s_compl
  //   rotr
  //   shiftr
  //   rsvd
endmodule

module c6s6_add1_8b_impl (
  input  [7:0] Input_bus_1,
  output [7:0] y_plus_1,
  output carry_out,
  output overflow
);

  c6s2_full_adder_8b_impl c6s2_full_adder_8b_impl_1 (
    .carry_in(1'b0), .x(8'h1), .y(Input_bus_1), .x_plus_y(y_plus_1), .carry_out(carry_out),
    .overflow(overflow));
endmodule

module c6s5_reg_8b_impl (
  input  [7:0] data_in,
  output [7:0] data_out
);

  wire clock_1_out;

  D_Flip_Flop d_ff_1 (.D(data_in[4]), .clk(clock_1_out), .Q(data_out[4]));  // open: Qn, preset, reset
  D_Flip_Flop d_ff_2 (.D(data_in[5]), .clk(clock_1_out), .Q(data_out[5]));  // open: Qn, preset, reset
  D_Flip_Flop d_ff_3 (.D(data_in[6]), .clk(clock_1_out), .Q(data_out[6]));  // open: Qn, preset, reset
  D_Flip_Flop d_ff_4 (.D(data_in[7]), .clk(clock_1_out), .Q(data_out[7]));  // open: Qn, preset, reset
  Clock clock_1 (.out(clock_1_out));
  D_Flip_Flop d_ff_5 (.D(data_in[0]), .clk(clock_1_out), .Q(data_out[0]));  // open: Qn, preset, reset
  D_Flip_Flop d_ff_6 (.D(data_in[1]), .clk(clock_1_out), .Q(data_out[1]));  // open: Qn, preset, reset
  D_Flip_Flop d_ff_7 (.D(data_in[2]), .clk(clock_1_out), .Q(data_out[2]));  // open: Qn, preset, reset
  D_Flip_Flop d_ff_8 (.D(data_in[3]), .clk(clock_1_out), .Q(data_out[3]));  // open: Qn, preset, reset
endmodule

module c6s6_ram_2x8_impl (
  input  WE,
  input  RE,
  input  [7:0] data_in,
  input  [1:0] addr,
  output [7:0] data_out
);

  wire and_1_out, and_2_out, and_3_out, and_4_out, decoder_1_out0, decoder_1_out1, decoder_1_out2,
       decoder_1_out3;
  wire [7:0] c6s5_reg_8b_impl_1_data_out, c6s5_reg_8b_impl_2_data_out, c6s5_reg_8b_impl_3_data_out,
       c6s5_reg_8b_impl_4_data_out, demultiplexer_1_out0, demultiplexer_1_out1, demultiplexer_1_out2,
       demultiplexer_1_out3, multiplexer_1_out, multiplexer_2_out, multiplexer_3_out, multiplexer_4_out,
       multiplexer_5_out;

  Demultiplexer #(.select(2), .width(8)) demultiplexer_1 (
    .out0(demultiplexer_1_out0), .out1(demultiplexer_1_out1), .out2(demultiplexer_1_out2),
    .out3(demultiplexer_1_out3), .in(data_in), .sel(addr));
  Decoder #(.select(2)) decoder_1 (
    .out0(decoder_1_out0), .out1(decoder_1_out1), .out2(decoder_1_out2), .out3(decoder_1_out3), .sel(addr),
    .en(1'b1));
  Multiplexer #(.width(8)) multiplexer_1 (
    .in0(c6s5_reg_8b_impl_1_data_out), .in1(demultiplexer_1_out0), .out(multiplexer_1_out), .sel(and_1_out));
  and and_1 (and_1_out, WE, decoder_1_out0);
  Multiplexer #(.width(8)) multiplexer_2 (
    .in0(c6s5_reg_8b_impl_3_data_out), .in1(demultiplexer_1_out2), .out(multiplexer_2_out), .sel(and_2_out));
  and and_2 (and_2_out, WE, decoder_1_out2);
  Multiplexer #(.width(8)) multiplexer_3 (
    .in0(c6s5_reg_8b_impl_2_data_out), .in1(demultiplexer_1_out1), .out(multiplexer_3_out), .sel(and_3_out));
  and and_3 (and_3_out, WE, decoder_1_out1);
  Multiplexer #(.width(8)) multiplexer_4 (
    .in0(c6s5_reg_8b_impl_4_data_out), .in1(demultiplexer_1_out3), .out(multiplexer_4_out), .sel(and_4_out));
  and and_4 (and_4_out, WE, decoder_1_out3);
  c6s5_reg_8b_impl c6s5_reg_8b_impl_1 (.data_in(multiplexer_1_out), .data_out(c6s5_reg_8b_impl_1_data_out));
  c6s5_reg_8b_impl c6s5_reg_8b_impl_2 (.data_in(multiplexer_3_out), .data_out(c6s5_reg_8b_impl_2_data_out));
  c6s5_reg_8b_impl c6s5_reg_8b_impl_3 (.data_in(multiplexer_2_out), .data_out(c6s5_reg_8b_impl_3_data_out));
  c6s5_reg_8b_impl c6s5_reg_8b_impl_4 (.data_in(multiplexer_4_out), .data_out(c6s5_reg_8b_impl_4_data_out));
  Multiplexer #(.select(2), .width(8)) multiplexer_5 (
    .in0(c6s5_reg_8b_impl_1_data_out), .in1(c6s5_reg_8b_impl_2_data_out), .in2(c6s5_reg_8b_impl_3_data_out),
    .in3(c6s5_reg_8b_impl_4_data_out), .out(multiplexer_5_out), .sel(addr));
  Multiplexer #(.width(8)) multiplexer_6 (.in0({8{1'b0}}), .in1(multiplexer_5_out), .out(data_out), .sel(RE));
endmodule

module c6s6_ram_4x8_impl (
  input  WE,
  input  RE,
  input  [7:0] data_in,
  input  [3:0] addr,
  output [7:0] data_out
);

  wire demultiplexer_1_out0, demultiplexer_1_out1, demultiplexer_1_out2, demultiplexer_1_out3;
  wire [1:0] demultiplexer_2_out0, demultiplexer_2_out1, demultiplexer_2_out2, demultiplexer_2_out3;
  wire [7:0] c6s6_ram_2x8_impl_1_data_out, c6s6_ram_2x8_impl_2_data_out, c6s6_ram_2x8_impl_3_data_out,
       c6s6_ram_2x8_impl_4_data_out;

  Demultiplexer #(.select(2)) demultiplexer_1 (
    .out0(demultiplexer_1_out0), .out1(demultiplexer_1_out1), .out2(demultiplexer_1_out2),
    .out3(demultiplexer_1_out3), .in(WE), .sel(addr[3:2]));
  Demultiplexer #(.select(2), .width(2)) demultiplexer_2 (
    .out0(demultiplexer_2_out0), .out1(demultiplexer_2_out1), .out2(demultiplexer_2_out2),
    .out3(demultiplexer_2_out3), .in(addr[1:0]), .sel(addr[3:2]));
  c6s6_ram_2x8_impl c6s6_ram_2x8_impl_1 (
    .WE(demultiplexer_1_out0), .RE(RE), .data_in(data_in), .addr(demultiplexer_2_out0),
    .data_out(c6s6_ram_2x8_impl_1_data_out));
  c6s6_ram_2x8_impl c6s6_ram_2x8_impl_2 (
    .WE(demultiplexer_1_out1), .RE(RE), .data_in(data_in), .addr(demultiplexer_2_out1),
    .data_out(c6s6_ram_2x8_impl_2_data_out));
  c6s6_ram_2x8_impl c6s6_ram_2x8_impl_3 (
    .WE(demultiplexer_1_out2), .RE(RE), .data_in(data_in), .addr(demultiplexer_2_out2),
    .data_out(c6s6_ram_2x8_impl_3_data_out));
  c6s6_ram_2x8_impl c6s6_ram_2x8_impl_4 (
    .WE(demultiplexer_1_out3), .RE(RE), .data_in(data_in), .addr(demultiplexer_2_out3),
    .data_out(c6s6_ram_2x8_impl_4_data_out));
  Multiplexer #(.select(2), .width(8)) multiplexer_1 (
    .in0(c6s6_ram_2x8_impl_1_data_out), .in1(c6s6_ram_2x8_impl_2_data_out),
    .in2(c6s6_ram_2x8_impl_3_data_out), .in3(c6s6_ram_2x8_impl_4_data_out), .out(data_out), .sel(addr[3:2]));
endmodule

module c6s6_ram_6x8_impl (
  input  WE,
  input  RE,
  input  [7:0] data_in,
  input  [5:0] addr,
  output [7:0] data_out
);

  wire demultiplexer_1_out0, demultiplexer_1_out1, demultiplexer_1_out2, demultiplexer_1_out3;
  wire [3:0] demultiplexer_2_out0, demultiplexer_2_out1, demultiplexer_2_out2, demultiplexer_2_out3;
  wire [7:0] c6s6_ram_4x8_impl_1_data_out, c6s6_ram_4x8_impl_2_data_out, c6s6_ram_4x8_impl_3_data_out,
       c6s6_ram_4x8_impl_4_data_out;

  Demultiplexer #(.select(2)) demultiplexer_1 (
    .out0(demultiplexer_1_out0), .out1(demultiplexer_1_out1), .out2(demultiplexer_1_out2),
    .out3(demultiplexer_1_out3), .in(WE), .sel(addr[5:4]));
  Demultiplexer #(.select(2), .width(4)) demultiplexer_2 (
    .out0(demultiplexer_2_out0), .out1(demultiplexer_2_out1), .out2(demultiplexer_2_out2),
    .out3(demultiplexer_2_out3), .in(addr[3:0]), .sel(addr[5:4]));
  c6s6_ram_4x8_impl c6s6_ram_4x8_impl_1 (
    .WE(demultiplexer_1_out0), .RE(RE), .data_in(data_in), .addr(demultiplexer_2_out0),
    .data_out(c6s6_ram_4x8_impl_1_data_out));
  c6s6_ram_4x8_impl c6s6_ram_4x8_impl_2 (
    .WE(demultiplexer_1_out1), .RE(RE), .data_in(data_in), .addr(demultiplexer_2_out1),
    .data_out(c6s6_ram_4x8_impl_2_data_out));
  c6s6_ram_4x8_impl c6s6_ram_4x8_impl_3 (
    .WE(demultiplexer_1_out2), .RE(RE), .data_in(data_in), .addr(demultiplexer_2_out2),
    .data_out(c6s6_ram_4x8_impl_3_data_out));
  c6s6_ram_4x8_impl c6s6_ram_4x8_impl_4 (
    .WE(demultiplexer_1_out3), .RE(RE), .data_in(data_in), .addr(demultiplexer_2_out3),
    .data_out(c6s6_ram_4x8_impl_4_data_out));
  Multiplexer #(.select(2), .width(8)) multiplexer_1 (
    .in0(c6s6_ram_4x8_impl_1_data_out), .in1(c6s6_ram_4x8_impl_2_data_out),
    .in2(c6s6_ram_4x8_impl_3_data_out), .in3(c6s6_ram_4x8_impl_4_data_out), .out(data_out), .sel(addr[5:4]));
endmodule

module c6s6_stepper_impl (
  input  reset,
  output s1,
  output s2,
  output s3,
  output s4,
  output s5,
  output s6,
  output s7,
  output s8
);

  wire clock_1_out;
  wire [2:0] c5s4_sync_up_counter_impl_1_y0;

  Clock clock_1 (.out(clock_1_out));
  c5s4_sync_up_counter_impl c5s4_sync_up_counter_impl_1 (
    .clk(clock_1_out), .R(reset), .y2(c5s4_sync_up_counter_impl_1_y0[2]),
    .y1(c5s4_sync_up_counter_impl_1_y0[1]), .y0(c5s4_sync_up_counter_impl_1_y0[0]));
  Decoder #(.select(3)) decoder_1 (
    .out0(s1), .out1(s2), .out2(s3), .out3(s4), .out4(s5), .out5(s6), .out6(s7), .out7(s8),
    .sel(c5s4_sync_up_counter_impl_1_y0), .en(1'b1));
endmodule

module c6s6_cpu_8b_impl (
  input  [3:0] alu_inst,
  input  [7:0] alu_in1,
  input  [7:0] alu_in2,
  output [7:0] alu_out,
  output [3:0] alu_flags
);

  c6s4_alu_8b_impl c6s4_alu_8b_impl_1 (.inst(alu_inst), .a(alu_in1), .b(alu_in2), .c(alu_out), .flags(alu_flags));
endmodule

module c6s6_reg_3x8_impl (
  input  WE,
  input  RE,
  input  [7:0] data_in,
  input  [2:0] addr,
  output [7:0] data_out
);

  wire demultiplexer_1_out0, demultiplexer_1_out1;
  wire [1:0] demultiplexer_2_out0, demultiplexer_2_out1;
  wire [7:0] c6s6_ram_2x8_impl_1_data_out, c6s6_ram_2x8_impl_2_data_out;

  Demultiplexer demultiplexer_1 (.out0(demultiplexer_1_out0), .out1(demultiplexer_1_out1), .in(WE), .sel(addr[2]));
  Demultiplexer #(.width(2)) demultiplexer_2 (
    .out0(demultiplexer_2_out0), .out1(demultiplexer_2_out1), .in(addr[1:0]), .sel(addr[2]));
  c6s6_ram_2x8_impl c6s6_ram_2x8_impl_1 (
    .WE(demultiplexer_1_out0), .RE(RE), .data_in(data_in), .addr(demultiplexer_2_out0),
    .data_out(c6s6_ram_2x8_impl_1_data_out));
  c6s6_ram_2x8_impl c6s6_ram_2x8_impl_2 (
    .WE(demultiplexer_1_out1), .RE(RE), .data_in(data_in), .addr(demultiplexer_2_out1),
    .data_out(c6s6_ram_2x8_impl_2_data_out));
  Multiplexer #(.width(8)) multiplexer_1 (
    .in0(c6s6_ram_2x8_impl_1_data_out), .in1(c6s6_ram_2x8_impl_2_data_out), .out(data_out), .sel(addr[2]));
endmodule

module c6s6_dx8 (
  input  [7:0] data,
  input  write,
  input  reset,
  input  [7:0] addr
);

  wire alu_bit, and_1_out, and_2_out, arg1, arg2, clock_1_out, clock_2_out, clock_3_out, clock_4_out, exec,
       load, load_aluOUT, load_val, or_1_out, RAM_WE, regDA_addr, regFileWE, s2, s3, s4, s5, s8, setIP,
       Stepper_s1, Stepper_s2, Stepper_s3, Stepper_s4, Stepper_s5, Stepper_s6, Stepper_s7, Stepper_s8, store;
  wire [2:0] multiplexer_7_out, multiplexer_8_out, regFileAddr;
  wire [3:0] ALU_alu_flags, aluFLG, inst;
  wire [7:0] ALU_alu_out, aluOUT, arg1_q, arg2_q, argAddr, data_t, ip, IPAdder_y_plus_1, memAddr,
       multiplexer_1_out, multiplexer_2_out, multiplexer_3_out, multiplexer_4_out, multiplexer_5_out,
       multiplexer_6_out, multiplexer_9_out, multiplexer_10_out, RAM_256B_data_out;

  LED RST (.in(reset));
  Multiplexer #(.width(8)) multiplexer_1 (.in0(ip), .in1(data_t), .out(multiplexer_1_out), .sel(store));
  Multiplexer #(.width(8)) multiplexer_2 (.in0(memAddr), .in1(argAddr), .out(multiplexer_2_out), .sel(s2));
  Register u_ip (.D(multiplexer_3_out), .en(s8), .clk(clock_1_out), .Q(memAddr), .clr(reset));
  Multiplexer #(.width(8)) multiplexer_3 (.in0(IPAdder_y_plus_1), .in1(ip), .out(multiplexer_3_out), .sel(setIP));
  Clock clock_1 (.out(clock_1_out));
  Multiplexer #(.width(8)) multiplexer_4 (.in0(multiplexer_1_out), .in1(data), .out(multiplexer_4_out), .sel(write));
  Multiplexer #(.width(8)) multiplexer_5 (.in0(multiplexer_6_out), .in1(addr), .out(multiplexer_5_out), .sel(write));
  Multiplexer #(.width(8)) multiplexer_6 (.in0(multiplexer_2_out), .in1(ip), .out(multiplexer_6_out), .sel(RAM_WE));
  or or_1 (or_1_out, write, RAM_WE);
  Multiplexer #(.width(3)) multiplexer_7 (.in0(3'b000), .in1(3'b001), .out(multiplexer_7_out), .sel(regDA_addr));
  c6s6_add1_8b_impl APAdder (.Input_bus_1(memAddr), .y_plus_1(argAddr));  // open: carry_out, overflow
  c6s5_ram_8x8_impl RAM_256B (
    .WE(or_1_out), .RE(1'b1), .data_in(multiplexer_4_out), .addr(multiplexer_5_out),
    .data_out(RAM_256B_data_out));
  Multiplexer #(.width(3)) multiplexer_8 (
    .in0(multiplexer_7_out), .in1(regFileAddr), .out(multiplexer_8_out), .sel(load));
  Multiplexer #(.width(8)) multiplexer_9 (
    .in0(RAM_256B_data_out), .in1(aluOUT), .out(multiplexer_9_out), .sel(load_aluOUT));
  Multiplexer #(.width(8)) multiplexer_10 (.in0(multiplexer_9_out), .in1(ip), .out(multiplexer_10_out), .sel(load_val));
  c6s6_add1_8b_impl IPAdder (.Input_bus_1(argAddr), .y_plus_1(IPAdder_y_plus_1));  // open: carry_out, overflow
  c6s6_reg_3x8_impl RegFile (
    .WE(regFileWE), .RE(1'b1), .data_in(multiplexer_10_out), .addr(multiplexer_8_out), .data_out(data_t));
  Register u_inst (.D(data_t), .en(s3), .clk(clock_2_out), .Q({alu_bit, inst, regFileAddr}), .clr(reset));
  Register u_arg1 (.D(data_t), .en(and_1_out), .clk(clock_2_out), .Q(arg1_q), .clr(reset));
  and and_1 (and_1_out, arg1, load);
  Register u_arg2 (.D(data_t), .en(and_2_out), .clk(clock_2_out), .Q(arg2_q), .clr(reset));
  and and_2 (and_2_out, load, arg2);
  Register arg (.D(data_t), .en(s4), .clk(clock_2_out), .Q(ip), .clr(reset));
  Clock clock_2 (.out(clock_2_out));
  c6s6_stepper_impl Stepper (
    .reset(reset), .s1(Stepper_s1), .s2(Stepper_s2), .s3(Stepper_s3), .s4(Stepper_s4), .s5(Stepper_s5),
    .s6(Stepper_s6), .s7(Stepper_s7), .s8(Stepper_s8));
  c6s6_cpu_8b_impl ALU (
    .alu_inst(inst), .alu_in1(arg1_q), .alu_in2(arg2_q), .alu_out(ALU_alu_out), .alu_flags(ALU_alu_flags));
  Register res (.D(ALU_alu_out), .en(s5), .clk(clock_3_out), .Q(aluOUT), .clr(reset));
  Clock clock_3 (.out(clock_3_out));
  Register #(.width(4)) flg (.D(ALU_alu_flags), .en(s5), .clk(clock_4_out), .Q(aluFLG), .clr(reset));
  Clock clock_4 (.out(clock_4_out));
  c6s6_controller_impl Controller (
    .s1(Stepper_s1), .s2(Stepper_s2), .s3(Stepper_s3), .s4(Stepper_s4), .s5(Stepper_s5), .s6(Stepper_s6),
    .s7(Stepper_s7), .s8(Stepper_s8), .alu_bit(alu_bit), .inst(inst), .aluFLG(aluFLG), .s2_out(s2),
    .s3_out(s3), .s4_out(s4), .s5_out(s5), .arg1(arg1), .arg2(arg2), .regDA_addr(regDA_addr),
    .RAM_WE(RAM_WE), .exec(exec), .load(load), .load_val(load_val), .load_aluOUT(load_aluOUT),
    .regFileWE(regFileWE), .store(store), .setIP(setIP));

  // Other names for the same wires on the sheet: maddr[7:0] = ip; val[7:0] = ip

  // Notes on the sheet:
  //   regDI : 000
  //   regDA : 001
  //   regIP : 010
  //   regA : 011
  //   regB : 100
  //   regOUT : 101
  //   regTMP : 110
  //   DX8 Computer
  //   by Ali Khudiyev
endmodule

module c6s6_controller_impl (
  input  alu_bit,
  input  [3:0] inst,
  input  [3:0] aluFLG,
  input  s1,
  input  s2,
  input  s3,
  input  s4,
  input  s5,
  input  s6,
  input  s7,
  input  s8,
  output regDA_addr,
  output RAM_WE,
  output exec,
  output load,
  output load_val,
  output load_aluOUT,
  output s2_out,
  output regFileWE,
  output s3_out,
  output s4_out,
  output store,
  output s5_out,
  output setIP,
  output arg1,
  output arg2
);

  wire and_1_out, and_8_out, and_9_out, and_10_out, and_11_out, and_12_out, and_13_out, and_14_out, load_t;

  and and_1 (and_1_out, alu_bit, s7);
  or or_1 (load, s7, s8);
  or or_2 (regFileWE, s2, s1, and_1_out, load_val);
  or or_3 (regDA_addr, s2, s4);
  or or_4 (exec, s5, s6);
  and and_2 (load_aluOUT, load, alu_bit);
  and and_3 (load_val, ~alu_bit, ~inst[3], ~inst[2], inst[1], ~inst[0]);  // AND_Gate
  and and_4 (arg1, ~alu_bit, ~inst[3], ~inst[2], inst[1], inst[0]);  // AND_Gate
  and and_5 (arg2, ~alu_bit, ~inst[3], inst[2], ~inst[1], ~inst[0]);  // AND_Gate
  and and_6 (store, ~alu_bit, ~inst[3], ~inst[2], ~inst[1], inst[0]);  // AND_Gate
  and and_7 (RAM_WE, store, load_t);
  and and_8 (and_8_out, ~alu_bit, ~inst[3], inst[2], ~inst[1], inst[0]);  // AND_Gate
  and and_9 (and_9_out, ~alu_bit, ~inst[3], inst[2], inst[1], ~inst[0]);  // AND_Gate
  and and_10 (and_10_out, ~alu_bit, ~inst[3], inst[2], inst[1], inst[0]);  // AND_Gate
  and and_11 (and_11_out, ~alu_bit, inst[3], ~inst[2], ~inst[1], ~inst[0]);  // AND_Gate
  and and_12 (and_12_out, and_9_out, aluFLG[3]);
  and and_13 (and_13_out, and_10_out, aluFLG[2]);
  and and_14 (and_14_out, and_11_out, aluFLG[1]);
  or or_5 (setIP, and_8_out, and_12_out, and_13_out, and_14_out);

  assign s2_out = s2;
  assign s3_out = s3;
  assign s4_out = s4;
  assign s5_out = s5;

  // Notes on the sheet:
  //   fetch
  //   decode
  //   execute
  //   load
endmodule
